# Fritzing sketch CO2 (saved by Fritzing 0.9.3b)
breadboards: 2

parts:
  TTP223B1 = TTP223B Capacitive Touch Sensor Module
  M1 = DOIT Esp32 DevKit v1 (30 pins long, 11 pins width) [part_number=ESP32S-PIN30]
  TD-er1 = MH-Z19 CO2 sensor [part_number=MH-Z19]
  TTP223B2 = TTP223B Capacitive Touch Sensor Module
  TTP223B3 = TTP223B Capacitive Touch Sensor Module
  F1 = Fan - Ventilador [package=THT]
  Bauteil1 = BME280 Breakout
  Squix1 = OLED 0.96" 128x64 I2C SSD1306

nets:
  GND: TTP223B1.GND, M1.GND, TD-er1.GND, TTP223B2.GND, TTP223B3.GND, F1.GND, Bauteil1.GND, Squix1.GND
  VCC: TTP223B1.VCC, M1.3V3, TTP223B2.VCC, TTP223B3.VCC, Bauteil1.3.3V, Squix1.VCC
  N1: TTP223B1.I/O, M1.D23
  N2: M1.RX2, TD-er1.SR
  N3: M1.TX2, TD-er1.TX
  N4: M1.D18, Bauteil1.SCK/SCL, Squix1.SCL
  N5: M1.D19, Bauteil1.SDI/SDA, Squix1.SCA
  N6: M1.D21, TTP223B3.I/O
  N7: M1.D22, TTP223B2.I/O
  VIN: M1.VIN, TD-er1.Vin, F1.5V

custom parts:
  DOIT Esp32 DevKit v1 (30 pins long, 11 pins width): The DOIT Esp32 DevKit v1 is one of the development board created by DOIT to evaluate the ESP-WROOM-32 module. It is based on the ESP32 microcontroller that boasts Wifi, Bluetooth, Ethernet and Low Power support all in a single chip. (vanepp) made breadboard work, adjusted pin numbering and labels and reduced size of schematic and cleaned up pcb. This chip is 30pins long (2 x15) and 11 pins width
  Fan - Ventilador: Ventilador de 2 pines, se encuentra comunmente en computadoras de escritorio
